# Fritzing sketch myLAB (saved by Fritzing 0.9.2b)

parts:
  Black_HAT1 = Black HAT Hack3r [form=male package=THT]
  Raspberry_Pi1 = Raspberry Pi 2  # not connected
  U1 = Explorer HAT Pro [part_number="Explorer HAT Pro" package=THT]
  U2 = Propeller HAT [part_number="Propeller HAT" package=THT]  # not connected

nets:
  N1: Black_HAT1.pin1, U1.POW3V3
  N2: Black_HAT1.pin2, U1.5v
  N3: Black_HAT1.pin3, U1.SDA
  N4: Black_HAT1.pin5, U1.SCL
  N5: Black_HAT1.pin6, U1.Ground
  N6: Black_HAT1.pin8, U1.RX
  N7: Black_HAT1.pin10, U1.TX
  N8: Black_HAT1.pin11, U1.PWM
  N9: Black_HAT1.pin19, U1.MISO
  N10: Black_HAT1.pin21, U1.MOSI
  N11: Black_HAT1.pin23, U1.SCK
  N12: Black_HAT1.pin24, U1.CS

notes:
  GPIO18 bridged to GPIO17
  as reset for Propeller HAT (brown cable)

custom parts:
  Black HAT Hack3r: Raspberry Pi GPIO breakout and HAT debugging area
  Explorer HAT Pro: Explorer HAT Pro with 4 Output and 4 Input connections, 4 Analog Inputs and 2 bi-directional motor channels, plus power and ground.
